// Logisim project 实验一.circ as structural Verilog: 5 circuits, main circuit 一位二进制全加器
module \一位二进制半加器  (
  input  A,
  input  B,
  output S,
  output C
);

  xor xor_1 (S, A, B);
  and and_1 (C, A, B);
endmodule

module \一位二进制全加器  (
  input  A,
  input  B,
  input  C0,
  output C,
  output S
);

  wire and_1_out, and_2_out, xor_1_out;

  and and_1 (and_1_out, A, B);
  xor xor_1 (xor_1_out, A, B);
  and and_2 (and_2_out, xor_1_out, C0);
  xor xor_2 (S, xor_1_out, C0);
  or or_1 (C, and_1_out, and_2_out);
endmodule

module \串行进位并行加法器  (
  input  A3,
  input  B3,
  input  A2,
  input  B2,
  input  A1,
  input  B1,
  input  A0,
  input  B0,
  input  C0,
  output C,
  output S3,
  output S2,
  output S1,
  output S0
);

  wire \一位二进制全加器_2_c , \一位二进制全加器_3_c , \一位二进制全加器_4_c ;

  \一位二进制全加器  \u_一位二进制全加器_1  (.A(A3), .C(C), .B(B3), .S(S3), .C0(\一位二进制全加器_2_c ));
  \一位二进制全加器  \u_一位二进制全加器_2  (.A(A2), .C(\一位二进制全加器_2_c ), .B(B2), .S(S2), .C0(\一位二进制全加器_3_c ));
  \一位二进制全加器  \u_一位二进制全加器_3  (.A(A1), .C(\一位二进制全加器_3_c ), .B(B1), .S(S1), .C0(\一位二进制全加器_4_c ));
  \一位二进制全加器  \u_一位二进制全加器_4  (.A(A0), .C(\一位二进制全加器_4_c ), .B(B0), .S(S0), .C0(C0));
endmodule

module \先行进位并行加法器  (
  input  C0,
  input  A0,
  input  B0,
  input  A1,
  input  B1,
  input  A2,
  input  B2,
  input  A3,
  input  B3,
  output S0,
  output S1,
  output S2,
  output S3,
  output C4
);

  wire and_1_out, and_2_out, and_3_out, and_4_out, and_5_out, and_6_out, and_7_out, and_8_out, and_9_out,
       and_10_out, C1_out, C2_out, C3_out, G0_out, G1_out, G2_out, G3_out, P0_out, P1_out, P2_out, P3_out;

  xor P0 (P0_out, A0, B0);
  and G0 (G0_out, A0, B0);
  xor P1 (P1_out, A1, B1);
  and G1 (G1_out, A1, B1);
  xor P2 (P2_out, A2, B2);
  and G2 (G2_out, A2, B2);
  xor P3 (P3_out, A3, B3);
  and G3 (G3_out, A3, B3);
  and and_1 (and_1_out, C0, P0_out);
  and and_2 (and_2_out, C0, P0_out, P1_out);
  and and_3 (and_3_out, P1_out, G0_out);
  and and_4 (and_4_out, C0, P0_out, P1_out, P2_out);
  and and_5 (and_5_out, P1_out, P2_out, G0_out);
  and and_6 (and_6_out, P2_out, G1_out);
  and and_7 (and_7_out, P2_out, P1_out, P0_out, C0, P3_out);
  and and_8 (and_8_out, G0_out, P3_out, P2_out, P1_out);
  and and_9 (and_9_out, G1_out, P3_out, P2_out);
  and and_10 (and_10_out, G2_out, P3_out);
  or C1 (C1_out, and_1_out, G0_out);
  or C2 (C2_out, and_2_out, and_3_out, G1_out);
  or C3 (C3_out, and_4_out, and_5_out, and_6_out, G2_out);
  or u_C4 (C4, and_7_out, and_8_out, and_9_out, and_10_out, G3_out);
  xor u_S0 (S0, C0, P0_out);
  xor u_S1 (S1, C1_out, P1_out);
  xor u_S2 (S2, C2_out, P2_out);
  xor u_S3 (S3, C3_out, P3_out);
endmodule

module \先行进位并行加法封装电路  (
  input  C0,
  input  A0,
  input  A1,
  input  A2,
  input  A3,
  input  B0,
  input  B1,
  input  B2,
  input  B3,
  output S0,
  output S1,
  output S2,
  output S3,
  output C4
);

  \先行进位并行加法器  \u_先行进位并行加法器_1  (
    .C0(C0), .A0(A0), .B0(B0), .A1(A1), .B1(B1), .A2(A2), .B2(B2), .A3(A3), .B3(B3), .S0(S0), .S1(S1),
    .S2(S2), .S3(S3), .C4(C4));
endmodule
