// Logisim project 实验三.circ as structural Verilog: 6 circuits, main circuit 四位乘法器
module \四位乘法器  (
  input  [3:0] A_3_0,
  input  [3:0] B_3_0,
  output [7:0] P_7_0
);

  wire [7:0] adder_1_out, adder_2_out, adder_3_out, adder_4_out, bit_extender_1_out, multiplexer_1_out,
       multiplexer_2_out, multiplexer_3_out, shifter_1_out, shifter_2_out, shifter_3_out;

  assign bit_extender_1_out = {{4{1'b0}}, B_3_0};  // Bit_Extender bit_extender_1
  Adder adder_1 (.a({8{1'b0}}), .b(bit_extender_1_out), .out(adder_1_out));  // open: cin, cout
  Shifter shifter_1 (.in(bit_extender_1_out), .\dist (3'b001), .out(shifter_1_out));
  Multiplexer #(.width(8)) multiplexer_1 (
    .in0({8{1'b0}}), .in1(adder_1_out), .out(multiplexer_1_out), .sel(A_3_0[0]));  // open: en
  Adder adder_2 (.a(multiplexer_1_out), .b(shifter_1_out), .out(adder_2_out));  // open: cin, cout
  Shifter shifter_2 (.in(shifter_1_out), .\dist (3'b001), .out(shifter_2_out));
  Multiplexer #(.width(8)) multiplexer_2 (
    .in0(multiplexer_1_out), .in1(adder_2_out), .out(multiplexer_2_out), .sel(A_3_0[1]));  // open: en
  Adder adder_3 (.a(multiplexer_2_out), .b(shifter_2_out), .out(adder_3_out));  // open: cin, cout
  Shifter shifter_3 (.in(shifter_2_out), .\dist (3'b001), .out(shifter_3_out));
  Multiplexer #(.width(8)) multiplexer_3 (
    .in0(multiplexer_2_out), .in1(adder_3_out), .out(multiplexer_3_out), .sel(A_3_0[2]));  // open: en
  Adder adder_4 (.a(multiplexer_3_out), .b(shifter_3_out), .out(adder_4_out));  // open: cin, cout
  Multiplexer #(.width(8)) multiplexer_4 (
    .in0(multiplexer_3_out), .in1(adder_4_out), .out(P_7_0), .sel(A_3_0[3]));  // open: en
endmodule

module \_32X4乘法器  (
  input  [3:0] A_3_0,
  input  [31:0] B_31_0,
  output [31:0] P_31_0
);

  wire [31:0] adder_1_out, adder_2_out, adder_3_out, adder_4_out, multiplexer_1_out, multiplexer_2_out,
       multiplexer_3_out, shifter_1_out, shifter_2_out, shifter_3_out;

  Adder #(.width(32)) adder_1 (.a({32{1'b0}}), .b(B_31_0), .out(adder_1_out));  // open: cin, cout
  Shifter #(.width(32)) shifter_1 (.in(B_31_0), .\dist (5'b00001), .out(shifter_1_out));
  Multiplexer #(.width(32)) multiplexer_1 (
    .in0({32{1'b0}}), .in1(adder_1_out), .out(multiplexer_1_out), .sel(A_3_0[0]));  // open: en
  Adder #(.width(32)) adder_2 (.a(multiplexer_1_out), .b(shifter_1_out), .out(adder_2_out));  // open: cin, cout
  Shifter #(.width(32)) shifter_2 (.in(shifter_1_out), .\dist (5'b00001), .out(shifter_2_out));
  Multiplexer #(.width(32)) multiplexer_2 (
    .in0(multiplexer_1_out), .in1(adder_2_out), .out(multiplexer_2_out), .sel(A_3_0[1]));  // open: en
  Adder #(.width(32)) adder_3 (.a(multiplexer_2_out), .b(shifter_2_out), .out(adder_3_out));  // open: cin, cout
  Shifter #(.width(32)) shifter_3 (.in(shifter_2_out), .\dist (5'b00001), .out(shifter_3_out));
  Multiplexer #(.width(32)) multiplexer_3 (
    .in0(multiplexer_2_out), .in1(adder_3_out), .out(multiplexer_3_out), .sel(A_3_0[2]));  // open: en
  Adder #(.width(32)) adder_4 (.a(multiplexer_3_out), .b(shifter_3_out), .out(adder_4_out));  // open: cin, cout
  Multiplexer #(.width(32)) multiplexer_4 (
    .in0(multiplexer_3_out), .in1(adder_4_out), .out(P_31_0), .sel(A_3_0[3]));  // open: en
endmodule

module \_32X32乘法器  (
  input  [31:0] A_31_0,
  input  [31:0] B_31_0,
  output [31:0] P_31_0
);

  wire [31:0] adder_1_out, adder_2_out, adder_3_out, adder_4_out, adder_5_out, adder_6_out,
       \n32x4乘法器_1_p_31_0 , \n32x4乘法器_2_p_31_0 , \n32x4乘法器_3_p_31_0 , \n32x4乘法器_4_p_31_0 ,
       \n32x4乘法器_5_p_31_0 , \n32x4乘法器_6_p_31_0 , \n32x4乘法器_7_p_31_0 , \n32x4乘法器_8_p_31_0 , shifter_1_out,
       shifter_2_out, shifter_3_out, shifter_4_out, shifter_5_out, shifter_6_out, shifter_7_out,
       shifter_8_out;

  \_32X4乘法器  \u_32x4乘法器_1  (.A_3_0(A_31_0[3:0]), .B_31_0(B_31_0), .P_31_0(\n32x4乘法器_1_p_31_0 ));
  \_32X4乘法器  \u_32x4乘法器_2  (.A_3_0(A_31_0[7:4]), .B_31_0(B_31_0), .P_31_0(\n32x4乘法器_2_p_31_0 ));
  \_32X4乘法器  \u_32x4乘法器_3  (.A_3_0(A_31_0[11:8]), .B_31_0(B_31_0), .P_31_0(\n32x4乘法器_3_p_31_0 ));
  \_32X4乘法器  \u_32x4乘法器_4  (.A_3_0(A_31_0[15:12]), .B_31_0(B_31_0), .P_31_0(\n32x4乘法器_4_p_31_0 ));
  \_32X4乘法器  \u_32x4乘法器_5  (.A_3_0(A_31_0[19:16]), .B_31_0(B_31_0), .P_31_0(\n32x4乘法器_5_p_31_0 ));
  \_32X4乘法器  \u_32x4乘法器_6  (.A_3_0(A_31_0[23:20]), .B_31_0(B_31_0), .P_31_0(\n32x4乘法器_6_p_31_0 ));
  \_32X4乘法器  \u_32x4乘法器_7  (.A_3_0(A_31_0[27:24]), .B_31_0(B_31_0), .P_31_0(\n32x4乘法器_7_p_31_0 ));
  \_32X4乘法器  \u_32x4乘法器_8  (.A_3_0(A_31_0[31:28]), .B_31_0(B_31_0), .P_31_0(\n32x4乘法器_8_p_31_0 ));
  Shifter #(.width(32)) shifter_1 (.in(\n32x4乘法器_1_p_31_0 ), .\dist ({5{1'b0}}), .out(shifter_1_out));
  Shifter #(.width(32)) shifter_2 (.in(\n32x4乘法器_2_p_31_0 ), .\dist (5'b00100), .out(shifter_2_out));
  Shifter #(.width(32)) shifter_3 (.in(\n32x4乘法器_3_p_31_0 ), .\dist (5'b01000), .out(shifter_3_out));
  Shifter #(.width(32)) shifter_4 (.in(\n32x4乘法器_4_p_31_0 ), .\dist (5'b01100), .out(shifter_4_out));
  Shifter #(.width(32)) shifter_5 (.in(\n32x4乘法器_5_p_31_0 ), .\dist (5'b10000), .out(shifter_5_out));
  Shifter #(.width(32)) shifter_6 (.in(\n32x4乘法器_6_p_31_0 ), .\dist (5'b10100), .out(shifter_6_out));
  Shifter #(.width(32)) shifter_7 (.in(\n32x4乘法器_7_p_31_0 ), .\dist (5'b11000), .out(shifter_7_out));
  Shifter #(.width(32)) shifter_8 (.in(\n32x4乘法器_8_p_31_0 ), .\dist (5'b11100), .out(shifter_8_out));
  Adder #(.width(32)) adder_1 (.a(shifter_1_out), .b(shifter_2_out), .out(adder_1_out));  // open: cin, cout
  Adder #(.width(32)) adder_2 (.a(shifter_3_out), .b(shifter_4_out), .out(adder_2_out));  // open: cin, cout
  Adder #(.width(32)) adder_3 (.a(shifter_5_out), .b(shifter_6_out), .out(adder_3_out));  // open: cin, cout
  Adder #(.width(32)) adder_4 (.a(shifter_7_out), .b(shifter_8_out), .out(adder_4_out));  // open: cin, cout
  Adder #(.width(32)) adder_5 (.a(adder_1_out), .b(adder_2_out), .out(adder_5_out));  // open: cin, cout
  Adder #(.width(32)) adder_6 (.a(adder_3_out), .b(adder_4_out), .out(adder_6_out));  // open: cin, cout
  Adder #(.width(32)) adder_7 (.a(adder_5_out), .b(adder_6_out), .out(P_31_0));  // open: cin, cout
endmodule

module \四位乘法器测试电路  (
  input  [3:0] A_3_0,
  input  [3:0] B_3_0,
  output [7:0] P_7_0,
  output [7:0] S_7_0
);

  wire [7:0] bit_extender_1_out, bit_extender_2_out, multiplier_1_out;

  assign bit_extender_1_out = {{4{1'b0}}, A_3_0};  // Bit_Extender bit_extender_1
  assign bit_extender_2_out = {{4{1'b0}}, B_3_0};  // Bit_Extender bit_extender_2
  \四位乘法器  \u_四位乘法器_1  (.A_3_0(A_3_0), .B_3_0(B_3_0), .P_7_0(P_7_0));
  Multiplier multiplier_1 (.a(bit_extender_1_out), .b(bit_extender_2_out), .out(multiplier_1_out));  // open: cin, cout
  assign S_7_0 = P_7_0 ^ multiplier_1_out;  // XOR_Gate xor_1, 8 bits wide
endmodule

module \_32X4乘法器测试电路  (
  input  [3:0] A_3_0,
  input  [31:0] B_31_0,
  output [31:0] P_31_0,
  output [31:0] S_31_0
);

  wire [31:0] bit_extender_1_out, multiplier_1_out;

  assign bit_extender_1_out = {{28{1'b0}}, A_3_0};  // Bit_Extender bit_extender_1
  \_32X4乘法器  \u_32x4乘法器_1  (.A_3_0(A_3_0), .B_31_0(B_31_0), .P_31_0(P_31_0));
  Multiplier #(.width(32)) multiplier_1 (
    .a(B_31_0), .b(bit_extender_1_out), .out(multiplier_1_out));  // open: cin, cout
  assign S_31_0 = P_31_0 ^ multiplier_1_out;  // XOR_Gate xor_1, 32 bits wide
endmodule

module \_32X32乘法器测试电路  (
  input  [31:0] A_31_0,
  input  [31:0] B_31_0,
  output [31:0] P_31_0,
  output [31:0] S_31_0
);

  wire [31:0] multiplier_1_out;

  \_32X32乘法器  \u_32x32乘法器_1  (.A_31_0(A_31_0), .B_31_0(B_31_0), .P_31_0(P_31_0));
  Multiplier #(.width(32)) multiplier_1 (.a(A_31_0), .b(B_31_0), .out(multiplier_1_out));  // open: cin, cout
  assign S_31_0 = P_31_0 ^ multiplier_1_out;  // XOR_Gate xor_1, 32 bits wide
endmodule
