// Logisim project 实验二.circ as structural Verilog: 9 circuits, main circuit 四位二进制可逆计数器
module \四位二进制可逆计数器  (
  input  CLR,
  input  nLD,
  input  D,
  input  C,
  input  B,
  input  A,
  input  CPU,
  input  CPD,
  output S3,
  output S2,
  output S1,
  output S0
);

  wire and_1_out, and_2_out, and_3_out, and_4_out, and_5_out, and_6_out, and_7_out, and_8_out, and_9_out,
       and_10_out, and_11_out, and_12_out, and_13_out, and_14_out, d_ff_1_qn, d_ff_2_qn, d_ff_3_qn,
       d_ff_4_qn, not_1_out, not_2_out, not_3_out, not_4_out, not_5_out, not_6_out, not_7_out, not_8_out,
       not_9_out, or_1_out, or_2_out, or_3_out, or_4_out, or_5_out, or_6_out, or_7_out, or_8_out;

  and and_1 (and_1_out, CPD, d_ff_2_qn, d_ff_3_qn, d_ff_4_qn);
  not not_1 (not_1_out, not_9_out);
  and and_2 (and_2_out, not_9_out, D);
  or or_1 (or_1_out, and_1_out, and_3_out);
  and and_3 (and_3_out, CPU, S2, S1, S0);
  D_Flip_Flop #(.trigger("falling")) d_ff_1 (
    .clk(or_1_out), .D(d_ff_1_qn), .Q(S3), .Qn(d_ff_1_qn), .preset(and_2_out), .en(not_1_out),
    .reset(or_2_out));
  or or_2 (or_2_out, and_4_out, CLR);
  and and_4 (and_4_out, not_2_out, not_9_out);
  not not_2 (not_2_out, D);
  and and_5 (and_5_out, CPD, d_ff_3_qn, d_ff_4_qn);
  not not_3 (not_3_out, not_9_out);
  and and_6 (and_6_out, not_9_out, C);
  or or_3 (or_3_out, and_5_out, and_7_out);
  and and_7 (and_7_out, CPU, S1, S0);
  D_Flip_Flop #(.trigger("falling")) d_ff_2 (
    .clk(or_3_out), .D(d_ff_2_qn), .Q(S2), .Qn(d_ff_2_qn), .preset(and_6_out), .en(not_3_out),
    .reset(or_4_out));
  or or_4 (or_4_out, and_8_out, CLR);
  and and_8 (and_8_out, not_4_out, not_9_out);
  not not_4 (not_4_out, C);
  and and_9 (and_9_out, CPD, d_ff_4_qn);
  not not_5 (not_5_out, not_9_out);
  and and_10 (and_10_out, not_9_out, B);
  or or_5 (or_5_out, and_9_out, and_11_out);
  and and_11 (and_11_out, CPU, S0);
  D_Flip_Flop #(.trigger("falling")) d_ff_3 (
    .clk(or_5_out), .D(d_ff_3_qn), .Q(S1), .Qn(d_ff_3_qn), .preset(and_10_out), .en(not_5_out),
    .reset(or_6_out));
  or or_6 (or_6_out, and_12_out, CLR);
  and and_12 (and_12_out, not_6_out, not_9_out);
  not not_6 (not_6_out, B);
  and and_13 (and_13_out, not_9_out, A);
  or or_7 (or_7_out, CPD, CPU);
  D_Flip_Flop #(.trigger("falling")) d_ff_4 (
    .clk(or_7_out), .D(d_ff_4_qn), .Q(S0), .Qn(d_ff_4_qn), .preset(and_13_out), .en(not_7_out),
    .reset(or_8_out));
  not not_7 (not_7_out, not_9_out);
  or or_8 (or_8_out, and_14_out, CLR);
  and and_14 (and_14_out, not_8_out, not_9_out);
  not not_8 (not_8_out, A);
  not not_9 (not_9_out, nLD);
endmodule

module \四位二进制可逆计数器测试电路  (
  input  CLR,
  input  [1:0] in_2,
  input  CPD,
  input  CPU,
  input  D,
  input  C,
  input  B,
  input  A,
  input  nLD,
  input  in_10,
  input  CPD_2,
  input  CPU_2,
  input  D_2,
  input  C_2,
  input  B_2,
  input  A_2,
  input  nLD_2,
  output S3,
  output S2,
  output S1,
  output S0
);

  wire and_1_out, and_2_out, multiplexer_1_out, or_1_out, \四位二进制可逆计数器_2_s0 , \四位二进制可逆计数器_2_s1 ,
       \四位二进制可逆计数器_2_s2 ;

  \四位二进制可逆计数器  \u_四位二进制可逆计数器_1  (
    .CLR(CLR), .CPD(CPD), .CPU(CPU), .nLD(nLD), .S0(S0), .S1(S1), .S2(S2), .S3(S3), .A(A), .B(B), .C(C), .D(D));
  or or_1 (or_1_out, multiplexer_1_out, in_10);
  \四位二进制可逆计数器  \u_四位二进制可逆计数器_2  (
    .CLR(or_1_out), .CPD(CPD_2), .CPU(CPU_2), .nLD(nLD_2), .S0(\四位二进制可逆计数器_2_s0 ), .S1(\四位二进制可逆计数器_2_s1 ),
    .S2(\四位二进制可逆计数器_2_s2 ), .A(A_2), .B(B_2), .C(C_2), .D(D_2));  // open: S3
  Multiplexer #(.select(2), .enable("false")) multiplexer_1 (
    .in0(\四位二进制可逆计数器_2_s2 ), .in1(and_1_out), .in2(and_2_out), .in3(\四位二进制可逆计数器_2_s0 ),
    .out(multiplexer_1_out), .sel(in_2));
  and and_1 (and_1_out, \四位二进制可逆计数器_2_s2 , \四位二进制可逆计数器_2_s1 );
  and and_2 (and_2_out, and_1_out, \四位二进制可逆计数器_2_s0 );
endmodule

module \二进制转8421码电路  (
  input  A0,
  input  A1,
  input  A2,
  input  A3,
  output S0,
  output S1,
  output S2,
  output S3,
  output S4,
  output S5,
  output S6,
  output S7
);

  wire and_1_out, or_1_out;

  or or_1 (or_1_out, A1, A2);
  and and_1 (and_1_out, or_1_out, A3);
  // 先行进位并行加法器 先行进位并行加法器_1: pin names not known; wires that end beside it: A0, A1, A2, A3, 1'b0, and_1_out, and_1_out, 1'b0, 1'b0, S4, S0, S1, S2, S3

  assign S5 = 1'b0;
  assign S6 = 1'b0;
  assign S7 = 1'b0;
endmodule

module \二进制转8421码测试电路  (
  input  in_1,
  input  in_2,
  input  in_3,
  input  in_4,
  output S7,
  output S6,
  output S5,
  output S4,
  output S3,
  output S2,
  output S1,
  output S0
);

  \二进制转8421码电路  \u_二进制转8421码电路_1  (
    .A0(in_4), .A1(in_3), .A2(in_2), .A3(in_1), .S0(S0), .S1(S1), .S2(S2), .S3(S3), .S4(S4), .S5(S5),
    .S6(S6), .S7(S7));
endmodule

module \显示电路  (
  input  A3,
  input  A2,
  input  A1,
  input  A0,
  output a,
  output b,
  output c,
  output d,
  output e,
  output f,
  output g
);

  wire and_1_out, and_2_out, and_3_out, and_4_out, and_5_out, and_6_out, and_7_out, and_8_out, and_9_out,
       and_10_out, and_11_out, and_12_out, and_13_out, and_14_out, and_15_out, and_16_out, and_17_out,
       and_18_out, and_19_out, not_1_out, not_2_out, not_3_out, not_4_out;

  not not_1 (not_1_out, A3);
  not not_2 (not_2_out, A2);
  not not_3 (not_3_out, A1);
  not not_4 (not_4_out, A0);
  and and_1 (and_1_out, A3, A0, not_3_out);
  and and_2 (and_2_out, A0, A2, not_1_out);
  and and_3 (and_3_out, not_1_out, not_2_out, A1);
  and and_4 (and_4_out, not_1_out, not_2_out);
  and and_5 (and_5_out, not_1_out, A1, A0);
  and and_6 (and_6_out, not_2_out, not_3_out);
  and and_7 (and_7_out, not_2_out, not_3_out, not_4_out);
  and and_8 (and_8_out, not_2_out, A0);
  and and_9 (and_9_out, not_1_out, A2);
  and and_10 (and_10_out, not_3_out, not_4_out);
  and and_11 (and_11_out, not_2_out, not_4_out);
  and and_12 (and_12_out, not_2_out, A1);
  and and_13 (and_13_out, not_3_out, A2, A0);
  and and_14 (and_14_out, A1, not_4_out);
  and and_15 (and_15_out, not_3_out, A2);
  and and_16 (and_16_out, not_3_out, A3);
  and and_17 (and_17_out, not_4_out, A2);
  and and_18 (and_18_out, not_2_out, A1);
  and and_19 (and_19_out, not_2_out, A3);
  or or_1 (a, and_1_out, and_2_out, and_3_out, and_7_out);
  or or_2 (b, and_4_out, and_5_out, and_6_out, and_10_out);
  or or_3 (c, and_6_out, and_8_out, and_9_out);
  or or_4 (d, and_11_out, and_12_out, and_13_out, and_14_out);
  or or_5 (e, and_7_out, and_14_out);
  or or_6 (f, and_10_out, and_15_out, and_16_out, and_17_out);
  or or_7 (g, and_15_out, and_14_out, and_18_out, and_19_out);
endmodule

module \显示电路测试电路  (
  input  in_1,
  input  in_2,
  input  in_3,
  input  in_4
);

  wire \二进制转8421码电路_1_s0 , \二进制转8421码电路_1_s1 , \二进制转8421码电路_1_s2 , \二进制转8421码电路_1_s3 , \二进制转8421码电路_1_s4 ,
       \二进制转8421码电路_1_s5 , \二进制转8421码电路_1_s6 , \二进制转8421码电路_1_s7 , \显示电路_1_a , \显示电路_1_b , \显示电路_1_c ,
       \显示电路_1_d , \显示电路_1_e , \显示电路_1_f , \显示电路_1_g , \显示电路_2_a , \显示电路_2_b , \显示电路_2_c , \显示电路_2_d ,
       \显示电路_2_e , \显示电路_2_f , \显示电路_2_g ;

  \二进制转8421码电路  \u_二进制转8421码电路_1  (
    .A0(in_4), .A1(in_3), .A2(in_2), .A3(in_1), .S0(\二进制转8421码电路_1_s0 ), .S1(\二进制转8421码电路_1_s1 ),
    .S2(\二进制转8421码电路_1_s2 ), .S3(\二进制转8421码电路_1_s3 ), .S4(\二进制转8421码电路_1_s4 ), .S5(\二进制转8421码电路_1_s5 ),
    .S6(\二进制转8421码电路_1_s6 ), .S7(\二进制转8421码电路_1_s7 ));
  \显示电路  \u_显示电路_1  (
    .a(\显示电路_1_a ), .b(\显示电路_1_b ), .c(\显示电路_1_c ), .d(\显示电路_1_d ), .e(\显示电路_1_e ), .f(\显示电路_1_f ),
    .g(\显示电路_1_g ), .A3(\二进制转8421码电路_1_s7 ), .A2(\二进制转8421码电路_1_s6 ), .A1(\二进制转8421码电路_1_s5 ),
    .A0(\二进制转8421码电路_1_s4 ));
  \显示电路  \u_显示电路_2  (
    .a(\显示电路_2_a ), .b(\显示电路_2_b ), .c(\显示电路_2_c ), .d(\显示电路_2_d ), .e(\显示电路_2_e ), .f(\显示电路_2_f ),
    .g(\显示电路_2_g ), .A3(\二进制转8421码电路_1_s3 ), .A2(\二进制转8421码电路_1_s2 ), .A1(\二进制转8421码电路_1_s1 ),
    .A0(\二进制转8421码电路_1_s0 ));
  _7_Segment_Display u_7_segment_display_1 (
    .g(\显示电路_1_g ), .f(\显示电路_1_f ), .a(\显示电路_1_a ), .b(\显示电路_1_b ), .e(\显示电路_1_e ), .d(\显示电路_1_d ),
    .c(\显示电路_1_c ));  // open: dp
  _7_Segment_Display u_7_segment_display_2 (
    .g(\显示电路_2_g ), .f(\显示电路_2_f ), .a(\显示电路_2_a ), .b(\显示电路_2_b ), .e(\显示电路_2_e ), .d(\显示电路_2_d ),
    .c(\显示电路_2_c ));  // open: dp
endmodule

module \报警电路  (
  input  CLR,
  input  CPD,
  input  CPU,
  output out_4,
  output out_5,
  output out_6,
  output out_7
);

  wire and_1_out, and_2_out, and_3_out, and_4_out, not_1_out, or_1_out;

  LED led_1 (.in(and_1_out));
  and and_1 (and_1_out, CPU, and_2_out);
  not not_1 (not_1_out, and_2_out);
  or or_1 (or_1_out, out_7, out_6, out_5, out_4);
  and and_2 (and_2_out, out_7, out_6, out_5, out_4);
  and and_3 (and_3_out, or_1_out, CPD);
  and and_4 (and_4_out, not_1_out, CPU);
  \四位二进制可逆计数器  \u_四位二进制可逆计数器_1  (
    .CLR(CLR), .CPD(and_3_out), .CPU(and_4_out), .nLD(1'b1), .S0(out_7), .S1(out_6), .S2(out_5), .S3(out_4),
    .A(1'b0), .B(1'b0), .C(1'b0), .D(1'b0));
endmodule

module \小型实验室门禁系统  (
  input  CLR,
  input  CPD,
  input  CPU,
  output out_4,
  output out_5,
  output out_6,
  output out_7,
  output out_8,
  output out_9,
  output out_10,
  output out_11,
  output out_12,
  output out_13,
  output out_14,
  output out_15,
  output out_16,
  output out_17,
  output out_18
);

  wire and_2_out, and_3_out, and_4_out, not_1_out, or_1_out, \二进制转8421码电路_1_s0 , \二进制转8421码电路_1_s1 ,
       \二进制转8421码电路_1_s2 , \二进制转8421码电路_1_s3 , \二进制转8421码电路_1_s4 , \二进制转8421码电路_1_s5 , \二进制转8421码电路_1_s6 ,
       \二进制转8421码电路_1_s7 , \四位二进制可逆计数器_1_s0 , \四位二进制可逆计数器_1_s1 , \四位二进制可逆计数器_1_s2 , \四位二进制可逆计数器_1_s3 ;

  and and_1 (out_10, CPU, and_2_out);
  not not_1 (not_1_out, and_2_out);
  or or_1 (or_1_out, \四位二进制可逆计数器_1_s0 , \四位二进制可逆计数器_1_s1 , \四位二进制可逆计数器_1_s2 , \四位二进制可逆计数器_1_s3 );
  and and_2 (and_2_out, \四位二进制可逆计数器_1_s0 , \四位二进制可逆计数器_1_s1 , \四位二进制可逆计数器_1_s2 , \四位二进制可逆计数器_1_s3 );
  and and_3 (and_3_out, or_1_out, CPD);
  and and_4 (and_4_out, not_1_out, CPU);
  \四位二进制可逆计数器  \u_四位二进制可逆计数器_1  (
    .CLR(CLR), .CPD(and_3_out), .CPU(and_4_out), .nLD(1'b1), .S0(\四位二进制可逆计数器_1_s0 ), .S1(\四位二进制可逆计数器_1_s1 ),
    .S2(\四位二进制可逆计数器_1_s2 ), .S3(\四位二进制可逆计数器_1_s3 ), .A(1'b0), .B(1'b0), .C(1'b0), .D(1'b0));
  \二进制转8421码电路  \u_二进制转8421码电路_1  (
    .A0(\四位二进制可逆计数器_1_s0 ), .A1(\四位二进制可逆计数器_1_s1 ), .A2(\四位二进制可逆计数器_1_s2 ), .A3(\四位二进制可逆计数器_1_s3 ),
    .S0(\二进制转8421码电路_1_s0 ), .S1(\二进制转8421码电路_1_s1 ), .S2(\二进制转8421码电路_1_s2 ), .S3(\二进制转8421码电路_1_s3 ),
    .S4(\二进制转8421码电路_1_s4 ), .S5(\二进制转8421码电路_1_s5 ), .S6(\二进制转8421码电路_1_s6 ), .S7(\二进制转8421码电路_1_s7 ));
  \显示电路  \u_显示电路_1  (
    .a(out_4), .b(out_5), .c(out_6), .d(out_7), .e(out_8), .f(out_9), .g(out_11), .A3(\二进制转8421码电路_1_s7 ),
    .A2(\二进制转8421码电路_1_s6 ), .A1(\二进制转8421码电路_1_s5 ), .A0(\二进制转8421码电路_1_s4 ));
  \显示电路  \u_显示电路_2  (
    .a(out_12), .b(out_13), .c(out_14), .d(out_15), .e(out_16), .f(out_17), .g(out_18),
    .A3(\二进制转8421码电路_1_s3 ), .A2(\二进制转8421码电路_1_s2 ), .A1(\二进制转8421码电路_1_s1 ), .A0(\二进制转8421码电路_1_s0 ));
endmodule

module \小型门禁系统测试电路  (
  input  in_1,
  input  in_2,
  input  in_3
);

  wire \小型实验室门禁系统_1_out_4 , \小型实验室门禁系统_1_out_5 , \小型实验室门禁系统_1_out_6 , \小型实验室门禁系统_1_out_7 ,
       \小型实验室门禁系统_1_out_8 , \小型实验室门禁系统_1_out_9 , \小型实验室门禁系统_1_out_10 , \小型实验室门禁系统_1_out_11 ,
       \小型实验室门禁系统_1_out_12 , \小型实验室门禁系统_1_out_13 , \小型实验室门禁系统_1_out_14 , \小型实验室门禁系统_1_out_15 ,
       \小型实验室门禁系统_1_out_16 , \小型实验室门禁系统_1_out_17 , \小型实验室门禁系统_1_out_18 ;

  \小型实验室门禁系统  \u_小型实验室门禁系统_1  (
    .CLR(in_1), .CPD(in_3), .CPU(in_2), .out_4(\小型实验室门禁系统_1_out_4 ), .out_5(\小型实验室门禁系统_1_out_5 ),
    .out_6(\小型实验室门禁系统_1_out_6 ), .out_7(\小型实验室门禁系统_1_out_7 ), .out_8(\小型实验室门禁系统_1_out_8 ),
    .out_9(\小型实验室门禁系统_1_out_9 ), .out_11(\小型实验室门禁系统_1_out_11 ), .out_12(\小型实验室门禁系统_1_out_12 ),
    .out_13(\小型实验室门禁系统_1_out_13 ), .out_14(\小型实验室门禁系统_1_out_14 ), .out_15(\小型实验室门禁系统_1_out_15 ),
    .out_16(\小型实验室门禁系统_1_out_16 ), .out_17(\小型实验室门禁系统_1_out_17 ), .out_18(\小型实验室门禁系统_1_out_18 ),
    .out_10(\小型实验室门禁系统_1_out_10 ));
  _7_Segment_Display u_7_segment_display_1 (
    .g(\小型实验室门禁系统_1_out_11 ), .f(\小型实验室门禁系统_1_out_9 ), .a(\小型实验室门禁系统_1_out_4 ), .b(\小型实验室门禁系统_1_out_5 ),
    .e(\小型实验室门禁系统_1_out_8 ), .d(\小型实验室门禁系统_1_out_7 ), .c(\小型实验室门禁系统_1_out_6 ));  // open: dp
  _7_Segment_Display u_7_segment_display_2 (
    .g(\小型实验室门禁系统_1_out_18 ), .f(\小型实验室门禁系统_1_out_17 ), .a(\小型实验室门禁系统_1_out_12 ), .b(\小型实验室门禁系统_1_out_13 ),
    .e(\小型实验室门禁系统_1_out_16 ), .d(\小型实验室门禁系统_1_out_15 ), .c(\小型实验室门禁系统_1_out_14 ));  // open: dp
  LED led_1 (.in(\小型实验室门禁系统_1_out_10 ));
endmodule
