// Logisim project 实验五.circ as structural Verilog: 14 circuits, main circuit 四位二进制可逆计数器
module \四位二进制可逆计数器  (
  input  CLR,
  input  \置9 ,
  input  CPU,
  input  CPD,
  output S3,
  output S2,
  output S1,
  output S0,
  output \进位 ,
  output \借位 
);

  wire and_1_out, and_2_out, and_3_out, and_4_out, and_5_out, and_6_out, and_7_out, and_8_out, and_9_out,
       and_10_out, and_11_out, and_12_out, and_13_out, and_14_out, and_15_out, d_ff_1_qn, d_ff_2_qn,
       d_ff_3_qn, d_ff_4_qn, not_1_out, not_2_out, not_3_out, not_4_out, not_5_out, not_6_out, not_7_out,
       not_8_out, not_9_out, not_10_out, not_11_out, or_1_out, or_2_out, or_3_out, or_4_out, or_5_out,
       or_6_out, or_7_out, or_8_out;

  and and_1 (and_1_out, and_15_out, d_ff_2_qn, d_ff_3_qn, d_ff_4_qn);
  not not_1 (not_1_out, \置9 );
  and and_2 (and_2_out, \置9 , 1'b1);
  or or_1 (or_1_out, and_1_out, and_3_out);
  and and_3 (and_3_out, CPU, S2, S1, S0);
  D_Flip_Flop #(.trigger("falling")) d_ff_1 (
    .clk(or_1_out), .D(d_ff_1_qn), .Q(S3), .Qn(d_ff_1_qn), .preset(and_2_out), .en(not_1_out),
    .reset(or_2_out));
  or or_2 (or_2_out, and_4_out, CLR);
  and and_4 (and_4_out, not_2_out, \置9 );
  not not_2 (not_2_out, 1'b1);
  and and_5 (and_5_out, and_15_out, d_ff_3_qn, d_ff_4_qn);
  not not_3 (not_3_out, \置9 );
  and and_6 (and_6_out, \置9 , 1'b0);
  or or_3 (or_3_out, and_5_out, and_7_out);
  and and_7 (and_7_out, CPU, S1, S0);
  D_Flip_Flop #(.trigger("falling")) d_ff_2 (
    .clk(or_3_out), .D(d_ff_2_qn), .Q(S2), .Qn(d_ff_2_qn), .preset(and_6_out), .en(not_3_out),
    .reset(or_4_out));
  or or_4 (or_4_out, and_8_out, CLR);
  and and_8 (and_8_out, not_4_out, \置9 );
  not not_4 (not_4_out, 1'b0);
  and and_9 (and_9_out, and_15_out, d_ff_4_qn);
  not not_5 (not_5_out, \置9 );
  and and_10 (and_10_out, \置9 , 1'b0);
  or or_5 (or_5_out, and_9_out, and_11_out);
  and and_11 (and_11_out, CPU, S0);
  D_Flip_Flop #(.trigger("falling")) d_ff_3 (
    .clk(or_5_out), .D(d_ff_3_qn), .Q(S1), .Qn(d_ff_3_qn), .preset(and_10_out), .en(not_5_out),
    .reset(or_6_out));
  or or_6 (or_6_out, and_12_out, CLR);
  and and_12 (and_12_out, not_6_out, \置9 );
  not not_6 (not_6_out, 1'b0);
  and and_13 (and_13_out, \置9 , 1'b1);
  or or_7 (or_7_out, and_15_out, CPU);
  D_Flip_Flop #(.trigger("falling")) d_ff_4 (
    .clk(or_7_out), .D(d_ff_4_qn), .Q(S0), .Qn(d_ff_4_qn), .preset(and_13_out), .en(not_7_out),
    .reset(or_8_out));
  or or_8 (or_8_out, and_14_out, CLR);
  not not_7 (not_7_out, \置9 );
  and and_14 (and_14_out, not_8_out, \置9 );
  not not_8 (not_8_out, 1'b1);
  and and_15 (and_15_out, not_9_out, CPD);
  nor nor_1 (\借位 , S0, S1, S2, S3);
  not not_9 (not_9_out, \借位 );
  not not_10 (not_10_out, S2);
  not not_11 (not_11_out, S0);
  and and_16 (\进位 , S3, not_10_out, S1, not_11_out);
endmodule

module \六十进制计数器  (
  input  CPU,
  input  Clr,
  input  Adj,
  input  CPD,
  output out_5,
  output out_6,
  output out_7,
  output out_8,
  output out_9,
  output out_10,
  output out_11,
  output out_12,
  output Qcc
);

  wire and_2_out, and_3_out, and_4_out, and_5_out, nand_1_out, not_1_out, not_2_out, or_1_out, or_2_out,
       \四位二进制可逆计数器_1_借位 , \四位二进制可逆计数器_2_借位 , \四位二进制可逆计数器_2_进位 ;

  and and_1 (Qcc, and_2_out, not_1_out);
  not not_1 (not_1_out, Adj);
  and and_2 (and_2_out, out_6, out_7);
  or or_1 (or_1_out, and_2_out, Clr);
  and and_3 (and_3_out, and_4_out, \四位二进制可逆计数器_2_借位 );
  \四位二进制可逆计数器  \u_四位二进制可逆计数器_1  (
    .CLR(or_1_out), .CPU(\四位二进制可逆计数器_2_进位 ), .CPD(and_3_out), .S3(out_5), .S2(out_6), .S1(out_7), .S0(out_8),
    .\借位 (\四位二进制可逆计数器_1_借位 ));  // open: 进位, 置9
  nand nand_1 (nand_1_out, \四位二进制可逆计数器_2_借位 , \四位二进制可逆计数器_1_借位 );
  and and_4 (and_4_out, nand_1_out, Adj, CPD);
  or or_2 (or_2_out, Clr, \四位二进制可逆计数器_2_进位 );
  not not_2 (not_2_out, CPD);
  and and_5 (and_5_out, and_3_out, not_2_out);
  \四位二进制可逆计数器  \u_四位二进制可逆计数器_2  (
    .CLR(or_2_out), .CPU(CPU), .CPD(and_4_out), .S3(out_9), .S2(out_10), .S1(out_11), .S0(out_12),
    .\进位 (\四位二进制可逆计数器_2_进位 ), .\借位 (\四位二进制可逆计数器_2_借位 ), .\置9 (and_5_out));
endmodule

module \六十进制计数器测试电路  (
  input  in_1
);

  wire button_1_out, button_2_out, clock_1_out, \六十进制计数器_1_qcc ;
  wire [3:0] \六十进制计数器_1_out_8 , \六十进制计数器_1_out_12 , \四位二进制可逆计数器_1_s0 ;

  Clock clock_1 (.out(clock_1_out));
  Button button_1 (.out(button_1_out));
  Hex_Digit_Display hex_digit_display_1 (.value(\六十进制计数器_1_out_8 ));  // open: dp
  Hex_Digit_Display hex_digit_display_2 (.value(\六十进制计数器_1_out_12 ));  // open: dp
  \六十进制计数器  \u_六十进制计数器_1  (
    .Clr(button_2_out), .CPU(clock_1_out), .out_9(\六十进制计数器_1_out_12 [3]), .out_10(\六十进制计数器_1_out_12 [2]),
    .out_11(\六十进制计数器_1_out_12 [1]), .out_12(\六十进制计数器_1_out_12 [0]), .Adj(in_1), .CPD(button_1_out),
    .out_5(\六十进制计数器_1_out_8 [3]), .out_6(\六十进制计数器_1_out_8 [2]), .out_7(\六十进制计数器_1_out_8 [1]),
    .out_8(\六十进制计数器_1_out_8 [0]), .Qcc(\六十进制计数器_1_qcc ));
  Button button_2 (.out(button_2_out));
  Hex_Digit_Display hex_digit_display_3 (.value(\四位二进制可逆计数器_1_s0 ));  // open: dp
  \四位二进制可逆计数器  \u_四位二进制可逆计数器_1  (
    .CLR(button_2_out), .CPU(\六十进制计数器_1_qcc ), .CPD(1'b0), .S3(\四位二进制可逆计数器_1_s0 [3]),
    .S2(\四位二进制可逆计数器_1_s0 [2]), .S1(\四位二进制可逆计数器_1_s0 [1]), .S0(\四位二进制可逆计数器_1_s0 [0]));  // open: 进位, 借位, 置9
endmodule

module \二十四进制的计数器电路  (
  input  set,
  input  in_2,
  input  in_3,
  input  in_4,
  input  in_5,
  output out_6,
  output out_7,
  output out_8,
  output out_9,
  output out_10,
  output out_11,
  output out_12,
  output out_13,
  output AM_FM,
  output Qcc
);

  wire and_1_out, and_2_out, and_3_out, comparator_1_eq, comparator_2_eq, not_1_out, not_2_out, or_1_out,
       or_2_out, subtractor_1_bout;
  wire [3:0] multiplexer_2_out, multiplexer_4_out, \二进制转8421码电路_1_p8 , \二进制转8421码电路_1_p12 ,
       \六十进制计数器_1_out_8 , \六十进制计数器_1_out_12 ;
  wire [7:0] adder_1_out, bit_extender_1_out, bit_extender_2_out, multiplier_1_out, \二进制转8421码电路_1_p4 ;

  // 二进制转8421码电路 二进制转8421码电路_1: pin names not known; wires that end beside it: \二进制转8421码电路_1_p4 [3], \二进制转8421码电路_1_p4 [2], \二进制转8421码电路_1_p4 [1], \二进制转8421码电路_1_p4 [0], \二进制转8421码电路_1_p8 [3], \二进制转8421码电路_1_p8 [2], \二进制转8421码电路_1_p8 [1], \二进制转8421码电路_1_p8 [0], \二进制转8421码电路_1_p12 [3], \二进制转8421码电路_1_p12 [2], \二进制转8421码电路_1_p12 [1], \二进制转8421码电路_1_p12 [0]
  Multiplexer #(.width(4), .enable("false")) multiplexer_1 (
    .in0(multiplexer_2_out), .in1(4'b0001), .out({out_6, out_7, out_8, out_9}), .sel(and_2_out));
  Multiplexer #(.width(4), .enable("false")) multiplexer_2 (
    .in0(\二进制转8421码电路_1_p8 ), .in1(\六十进制计数器_1_out_8 ), .out(multiplexer_2_out), .sel(or_2_out));
  not not_1 (not_1_out, in_3);
  and and_1 (and_1_out, in_3, in_4);
  Multiplexer #(.width(4), .enable("false")) multiplexer_3 (
    .in0(multiplexer_4_out), .in1(4'b0010), .out({out_10, out_11, out_12, out_13}), .sel(and_2_out));
  Comparator #(.width(4)) comparator_1 (.a(multiplexer_2_out), .b(4'b0000), .eq(comparator_1_eq));  // open: gt, lt
  Multiplexer #(.width(4), .enable("false")) multiplexer_4 (
    .in0(\二进制转8421码电路_1_p12 ), .in1(\六十进制计数器_1_out_12 ), .out(multiplexer_4_out), .sel(or_2_out));
  and and_2 (and_2_out, comparator_1_eq, comparator_2_eq, not_2_out);
  Comparator #(.width(4)) comparator_2 (.a(4'b0000), .b(multiplexer_4_out), .eq(comparator_2_eq));  // open: gt, lt
  assign bit_extender_1_out = {{4{1'b0}}, \六十进制计数器_1_out_8 };  // Bit_Extender bit_extender_1
  \六十进制计数器  \u_六十进制计数器_1  (
    .Clr(or_1_out), .CPU(in_2), .out_9(\六十进制计数器_1_out_12 [3]), .out_10(\六十进制计数器_1_out_12 [2]),
    .out_11(\六十进制计数器_1_out_12 [1]), .out_12(\六十进制计数器_1_out_12 [0]), .Adj(in_3), .CPD(and_1_out),
    .out_5(\六十进制计数器_1_out_8 [3]), .out_6(\六十进制计数器_1_out_8 [2]), .out_7(\六十进制计数器_1_out_8 [1]),
    .out_8(\六十进制计数器_1_out_8 [0]));  // open: Qcc
  or or_1 (or_1_out, and_3_out, in_5);
  not not_2 (not_2_out, set);
  or or_2 (or_2_out, set, subtractor_1_bout);
  Multiplier multiplier_1 (.a(8'ha), .b(bit_extender_1_out), .out(multiplier_1_out));  // open: cin, cout
  assign bit_extender_2_out = {{4{1'b0}}, \六十进制计数器_1_out_12 };  // Bit_Extender bit_extender_2
  and and_3 (and_3_out, \六十进制计数器_1_out_8 [1], \六十进制计数器_1_out_12 [2]);
  and and_4 (Qcc, and_3_out, not_1_out);
  Adder adder_1 (.a(multiplier_1_out), .b(bit_extender_2_out), .out(adder_1_out));  // open: cin, cout
  not not_3 (AM_FM, subtractor_1_bout);
  Subtractor subtractor_1 (.a(adder_1_out), .b(8'hc), .out(\二进制转8421码电路_1_p4 ), .bout(subtractor_1_bout));  // open: bin
endmodule

module \二十四进制的计数器电路测试电路  (
  input  in_1,
  input  in_2
);

  wire button_1_out, button_2_out, button_3_out, clock_1_out, \二十四进制的计数器电路_1_qcc ;
  wire [3:0] \二十四进制的计数器电路_1_out_9 , \二十四进制的计数器电路_1_out_13 , \四位二进制可逆计数器_1_s0 ;

  Clock clock_1 (.out(clock_1_out));
  Button button_1 (.out(button_1_out));
  Hex_Digit_Display hex_digit_display_1 (.value(\二十四进制的计数器电路_1_out_9 ));  // open: dp
  Hex_Digit_Display hex_digit_display_2 (.value(\二十四进制的计数器电路_1_out_13 ));  // open: dp
  \二十四进制的计数器电路  \u_二十四进制的计数器电路_1  (
    .in_2(clock_1_out), .in_4(in_1), .in_3(button_1_out), .Qcc(\二十四进制的计数器电路_1_qcc ), .set(in_2),
    .out_6(\二十四进制的计数器电路_1_out_9 [3]), .out_8(\二十四进制的计数器电路_1_out_9 [1]), .out_9(\二十四进制的计数器电路_1_out_9 [0]),
    .out_10(\二十四进制的计数器电路_1_out_13 [3]), .out_12(\二十四进制的计数器电路_1_out_13 [1]),
    .out_13(\二十四进制的计数器电路_1_out_13 [0]), .out_11(\二十四进制的计数器电路_1_out_13 [2]), .out_7(\二十四进制的计数器电路_1_out_9 [2]),
    .in_5(button_2_out));  // open: AM_FM
  Button button_2 (.out(button_2_out));
  Button button_3 (.out(button_3_out));
  Hex_Digit_Display hex_digit_display_3 (.value(\四位二进制可逆计数器_1_s0 ));  // open: dp
  \四位二进制可逆计数器  \u_四位二进制可逆计数器_1  (
    .CLR(button_3_out), .CPU(\二十四进制的计数器电路_1_qcc ), .CPD(1'b0), .S3(\四位二进制可逆计数器_1_s0 [3]),
    .S2(\四位二进制可逆计数器_1_s0 [2]), .S1(\四位二进制可逆计数器_1_s0 [1]), .S0(\四位二进制可逆计数器_1_s0 [0]));  // open: 进位, 借位, 置9
endmodule

module \上下午文字显示电路  (
  input  AM_FM,
  input  TT,
  output [4:0] out_3,
  output [4:0] out_4,
  output [4:0] out_5,
  output [4:0] out_6
);

  wire [19:0] multiplexer_1_out;

  Multiplexer #(.width(20), .enable("false")) multiplexer_1 (
    .in0(20'hfca1), .in1(20'h87e90), .out(multiplexer_1_out), .sel(AM_FM));
  Multiplexer #(.width(20), .enable("false")) multiplexer_2 (
    .in0({20{1'b0}}), .in1(multiplexer_1_out), .out({out_3, out_4, out_5, out_6}), .sel(TT));
endmodule

module \上下午文字显示测试电路  (
  input  in_1,
  input  in_2
);

  wire [4:0] \上下午文字显示电路_1_out_3 , \上下午文字显示电路_1_out_4 , \上下午文字显示电路_1_out_5 , \上下午文字显示电路_1_out_6 ;

  DotMatrix #(.matrixcols(4), .matrixrows(5)) dotmatrix_1 (
    .col0(\上下午文字显示电路_1_out_3 ), .col1(\上下午文字显示电路_1_out_4 ), .col2(\上下午文字显示电路_1_out_5 ),
    .col3(\上下午文字显示电路_1_out_6 ));
  \上下午文字显示电路  \u_上下午文字显示电路_1  (
    .out_3(\上下午文字显示电路_1_out_3 ), .out_4(\上下午文字显示电路_1_out_4 ), .out_5(\上下午文字显示电路_1_out_5 ),
    .out_6(\上下午文字显示电路_1_out_6 ), .AM_FM(in_1), .TT(in_2));
endmodule

module \电子钟整点报时电路  (
  input  Min_plus,
  input  Sec_plus,
  input  Hr_plus,
  input  in_4,
  input  in_5,
  input  Sec_minus,
  input  Min_minus,
  input  Hr_minus,
  input  in_9,
  output [3:0] out_10,
  output [3:0] out_11,
  output [3:0] out_12,
  output [3:0] out_13,
  output out_14,
  output [3:0] out_15,
  output [3:0] out_16,
  output AM_FM
);

  wire and_1_out, and_2_out, and_3_out, and_5_out, and_6_out, or_1_out, or_2_out, \六十进制计数器_1_qcc ,
       \六十进制计数器_2_qcc ;

  and and_1 (and_1_out, Sec_minus, in_4);
  \六十进制计数器  \u_六十进制计数器_1  (
    .Clr(in_9), .CPU(Sec_plus), .out_9(out_11[3]), .out_10(out_11[2]), .out_11(out_11[1]),
    .out_12(out_11[0]), .Adj(in_4), .CPD(and_1_out), .out_5(out_10[3]), .out_6(out_10[2]), .out_7(out_10[1]),
    .out_8(out_10[0]), .Qcc(\六十进制计数器_1_qcc ));
  and and_2 (and_2_out, Min_plus, in_4);
  and and_3 (and_3_out, Min_minus, in_4);
  or or_1 (or_1_out, and_2_out, \六十进制计数器_1_qcc );
  \六十进制计数器  \u_六十进制计数器_2  (
    .Clr(in_9), .CPU(or_1_out), .out_9(out_13[3]), .out_10(out_13[2]), .out_11(out_13[1]),
    .out_12(out_13[0]), .Adj(in_4), .CPD(and_3_out), .out_5(out_12[3]), .out_6(out_12[2]), .out_7(out_12[1]),
    .out_8(out_12[0]), .Qcc(\六十进制计数器_2_qcc ));
  and and_4 (out_14, out_12[2], out_12[0], out_13[3], out_13[0], out_10[2], out_10[0]);
  and and_5 (and_5_out, Hr_plus, in_4);
  and and_6 (and_6_out, Hr_minus, in_4);
  or or_2 (or_2_out, and_5_out, \六十进制计数器_2_qcc );
  \二十四进制的计数器电路  \u_二十四进制的计数器电路_1  (
    .in_2(or_2_out), .in_4(in_4), .in_3(and_6_out), .set(in_5), .out_6(out_15[3]), .out_8(out_15[1]),
    .out_9(out_15[0]), .out_10(out_16[3]), .out_12(out_16[1]), .out_13(out_16[0]), .out_11(out_16[2]),
    .out_7(out_15[2]), .AM_FM(AM_FM), .in_5(in_9));  // open: Qcc
endmodule

module \电子钟整点报时电路测试电路  (
  input  in_1,
  input  in_2
);

  wire button_1_out, button_2_out, button_3_out, button_4_out, button_5_out, button_6_out, clock_1_out,
       \电子钟整点报时电路_1_out_14 ;
  wire [3:0] \电子钟整点报时电路_1_out_10 , \电子钟整点报时电路_1_out_11 , \电子钟整点报时电路_1_out_12 , \电子钟整点报时电路_1_out_13 ,
       \电子钟整点报时电路_1_out_15 , \电子钟整点报时电路_1_out_16 ;

  Button button_1 (.out(button_1_out));
  Clock clock_1 (.out(clock_1_out));
  Button button_2 (.out(button_2_out));
  Button button_3 (.out(button_3_out));
  Button button_4 (.out(button_4_out));
  Button button_5 (.out(button_5_out));
  Button button_6 (.out(button_6_out));
  Hex_Digit_Display hex_digit_display_1 (.value(\电子钟整点报时电路_1_out_15 ));  // open: dp
  Hex_Digit_Display hex_digit_display_2 (.value(\电子钟整点报时电路_1_out_16 ));  // open: dp
  Hex_Digit_Display hex_digit_display_3 (.value(\电子钟整点报时电路_1_out_12 ));  // open: dp
  Hex_Digit_Display hex_digit_display_4 (.value(\电子钟整点报时电路_1_out_10 ));  // open: dp
  Hex_Digit_Display hex_digit_display_5 (.value(\电子钟整点报时电路_1_out_13 ));  // open: dp
  \电子钟整点报时电路  \u_电子钟整点报时电路_1  (
    .in_9(button_1_out), .Sec_plus(clock_1_out), .Hr_minus(button_6_out), .in_4(in_1),
    .out_14(\电子钟整点报时电路_1_out_14 ), .Hr_plus(button_5_out), .Min_plus(button_3_out), .Min_minus(button_4_out),
    .in_5(in_2), .out_16(\电子钟整点报时电路_1_out_16 ), .out_15(\电子钟整点报时电路_1_out_15 ), .out_10(\电子钟整点报时电路_1_out_10 ),
    .out_11(\电子钟整点报时电路_1_out_11 ), .out_12(\电子钟整点报时电路_1_out_12 ), .out_13(\电子钟整点报时电路_1_out_13 ),
    .Sec_minus(button_2_out));  // open: AM_FM
  Hex_Digit_Display hex_digit_display_6 (.value(\电子钟整点报时电路_1_out_11 ));  // open: dp
  LED led_1 (.in(\电子钟整点报时电路_1_out_14 ));
endmodule

module \秒脉冲产生电路  (
  input  in_1,
  output Qcc
);

  \四位二进制可逆计数器  \u_四位二进制可逆计数器_1  (.CLR(Qcc), .CPU(in_1), .CPD(1'b0), .S3(Qcc));  // open: S2, S1, S0, 进位, 借位, 置9
endmodule

module \多功能数字钟电路  (
  input  in_1,
  input  in_2,
  input  in_3,
  input  in_4,
  input  in_5,
  input  in_6,
  input  in_7,
  input  in_8,
  input  in_9,
  output [4:0] out_10,
  output [4:0] out_11,
  output [4:0] out_12,
  output [3:0] out_13,
  output [3:0] out_14,
  output [3:0] out_15,
  output [3:0] out_16,
  output [3:0] out_17,
  output [3:0] out_18,
  output [4:0] out_19,
  output out_20,
  output out_21
);

  wire \闹钟_1_out_21 ;

  and and_1 (out_21, \闹钟_1_out_21 , in_9);
  \闹钟  \u_闹钟_1  (
    .out_14(out_13), .out_15(out_14), .out_16(out_15), .out_17(out_16), .ON_OFF(in_8), .\闹钟 (out_20),
    .alarm(in_7), .Clr(in_5), .Adj0(in_1), .CP(in_9), .Adj1(in_2), .CPU(in_3), .CPD(in_4),
    .out_21(\闹钟_1_out_21 ), .in_9(in_6), .out_18(out_17), .out_19(out_18), .out_10(out_19), .out_11(out_12),
    .out_12(out_11), .out_13(out_10));
endmodule

module \多功能数字钟电路测试电路  (
  input  in_1,
  input  in_2,
  input  in_3,
  input  in_4,
  input  in_5
);

  wire button_1_out, button_2_out, button_3_out, clock_1_out, \多功能数字钟电路_1_out_20 , \多功能数字钟电路_1_out_21 ;
  wire [3:0] \多功能数字钟电路_1_out_13 , \多功能数字钟电路_1_out_14 , \多功能数字钟电路_1_out_15 , \多功能数字钟电路_1_out_16 ,
       \多功能数字钟电路_1_out_17 , \多功能数字钟电路_1_out_18 ;
  wire [4:0] \多功能数字钟电路_1_out_10 , \多功能数字钟电路_1_out_11 , \多功能数字钟电路_1_out_12 , \多功能数字钟电路_1_out_19 ;

  DotMatrix #(.matrixcols(4), .matrixrows(5)) dotmatrix_1 (
    .col0(\多功能数字钟电路_1_out_19 ), .col1(\多功能数字钟电路_1_out_12 ), .col2(\多功能数字钟电路_1_out_11 ),
    .col3(\多功能数字钟电路_1_out_10 ));
  Hex_Digit_Display hex_digit_display_1 (.value(\多功能数字钟电路_1_out_13 ));  // open: dp
  Button button_1 (.out(button_1_out));
  Button button_2 (.out(button_2_out));
  Clock clock_1 (.out(clock_1_out));
  Hex_Digit_Display hex_digit_display_2 (.value(\多功能数字钟电路_1_out_14 ));  // open: dp
  Hex_Digit_Display hex_digit_display_3 (.value(\多功能数字钟电路_1_out_15 ));  // open: dp
  Button button_3 (.out(button_3_out));
  Hex_Digit_Display hex_digit_display_4 (.value(\多功能数字钟电路_1_out_17 ));  // open: dp
  Hex_Digit_Display hex_digit_display_5 (.value(\多功能数字钟电路_1_out_16 ));  // open: dp
  Hex_Digit_Display hex_digit_display_6 (.value(\多功能数字钟电路_1_out_18 ));  // open: dp
  \多功能数字钟电路  \u_多功能数字钟电路_1  (
    .in_1(in_1), .in_2(in_2), .in_9(clock_1_out), .in_3(button_2_out), .in_4(button_1_out),
    .in_5(button_3_out), .in_6(in_3), .in_7(in_4), .in_8(in_5), .out_19(\多功能数字钟电路_1_out_19 ),
    .out_12(\多功能数字钟电路_1_out_12 ), .out_11(\多功能数字钟电路_1_out_11 ), .out_10(\多功能数字钟电路_1_out_10 ),
    .out_13(\多功能数字钟电路_1_out_13 ), .out_14(\多功能数字钟电路_1_out_14 ), .out_15(\多功能数字钟电路_1_out_15 ),
    .out_16(\多功能数字钟电路_1_out_16 ), .out_17(\多功能数字钟电路_1_out_17 ), .out_18(\多功能数字钟电路_1_out_18 ),
    .out_21(\多功能数字钟电路_1_out_21 ), .out_20(\多功能数字钟电路_1_out_20 ));
  LED led_1 (.in(\多功能数字钟电路_1_out_20 ));
  LED led_2 (.in(\多功能数字钟电路_1_out_21 ));
endmodule

module \闹钟  (
  input  ON_OFF,
  input  alarm,
  input  Clr,
  input  Adj0,
  input  CP,
  input  Adj1,
  input  CPU,
  input  CPD,
  input  in_9,
  output [4:0] out_10,
  output [4:0] out_11,
  output [4:0] out_12,
  output [4:0] out_13,
  output [3:0] out_14,
  output [3:0] out_15,
  output [3:0] out_16,
  output [3:0] out_17,
  output [3:0] out_18,
  output [3:0] out_19,
  output \闹钟 ,
  output out_21
);

  wire and_1_out, and_2_out, and_3_out, and_4_out, and_5_out, and_6_out, and_7_out, and_8_out,
       comparator_1_eq, multiplexer_5_out, nor_1_out, not_1_out, not_2_out, not_3_out, not_4_out, xnor_1_out,
       \电子钟整点报时电路_1_am_fm , \电子钟整点报时电路_2_am_fm , \秒脉冲产生电路_1_qcc ;
  wire [3:0] and_9_out, xnor_2_out, xnor_3_out, xnor_4_out, xnor_5_out, \电子钟整点报时电路_1_out_12 ,
       \电子钟整点报时电路_1_out_13 , \电子钟整点报时电路_1_out_15 , \电子钟整点报时电路_1_out_16 , \电子钟整点报时电路_2_out_12 ,
       \电子钟整点报时电路_2_out_13 , \电子钟整点报时电路_2_out_15 , \电子钟整点报时电路_2_out_16 ;

  not not_1 (not_1_out, alarm);
  not not_2 (not_2_out, Adj1);
  not not_3 (not_3_out, not_1_out);
  and and_1 (and_1_out, not_1_out, Clr);
  \秒脉冲产生电路  \u_秒脉冲产生电路_1  (.Qcc(\秒脉冲产生电路_1_qcc ), .in_1(CP));
  and and_2 (and_2_out, Adj1, CPU);
  and and_3 (and_3_out, Adj1, CPD);
  and and_4 (and_4_out, CPU, not_2_out);
  and and_5 (and_5_out, CPD, not_2_out);
  and and_6 (and_6_out, Clr, not_3_out);
  and and_7 (and_7_out, not_3_out, Adj0);
  and and_8 (and_8_out, not_1_out, Adj0);
  Multiplexer #(.width(4), .enable("false")) multiplexer_1 (
    .in0(\电子钟整点报时电路_1_out_15 ), .in1(\电子钟整点报时电路_2_out_15 ), .out(out_14), .sel(alarm));
  Multiplexer #(.width(4), .enable("false")) multiplexer_2 (
    .in0(\电子钟整点报时电路_1_out_16 ), .in1(\电子钟整点报时电路_2_out_16 ), .out(out_15), .sel(alarm));
  Multiplexer #(.width(4), .enable("false")) multiplexer_3 (
    .in0(\电子钟整点报时电路_1_out_13 ), .in1(\电子钟整点报时电路_2_out_13 ), .out(out_17), .sel(alarm));
  Multiplexer #(.width(4), .enable("false")) multiplexer_4 (
    .in0(\电子钟整点报时电路_1_out_12 ), .in1(\电子钟整点报时电路_2_out_12 ), .out(out_16), .sel(alarm));
  \电子钟整点报时电路  \u_电子钟整点报时电路_1  (
    .in_9(and_1_out), .Sec_plus(\秒脉冲产生电路_1_qcc ), .Hr_minus(and_5_out), .in_4(and_8_out), .out_14(out_21),
    .Hr_plus(and_4_out), .Min_plus(and_2_out), .Min_minus(and_3_out), .in_5(in_9),
    .out_16(\电子钟整点报时电路_1_out_16 ), .out_15(\电子钟整点报时电路_1_out_15 ), .out_10(out_18), .out_11(out_19),
    .out_12(\电子钟整点报时电路_1_out_12 ), .out_13(\电子钟整点报时电路_1_out_13 ), .AM_FM(\电子钟整点报时电路_1_am_fm ));  // open: Sec_minus
  \上下午文字显示电路  \u_上下午文字显示电路_1  (
    .out_3(out_10), .out_4(out_11), .out_5(out_12), .out_6(out_13), .AM_FM(multiplexer_5_out), .TT(not_4_out));
  Multiplexer #(.enable("false")) multiplexer_5 (
    .in0(\电子钟整点报时电路_1_am_fm ), .in1(\电子钟整点报时电路_2_am_fm ), .out(multiplexer_5_out), .sel(alarm));
  not not_4 (not_4_out, in_9);
  xnor xnor_1 (xnor_1_out, \电子钟整点报时电路_1_am_fm , \电子钟整点报时电路_2_am_fm );
  assign xnor_2_out = ~(\电子钟整点报时电路_1_out_15  ^ \电子钟整点报时电路_2_out_15 );  // XNOR_Gate xnor_2, 4 bits wide
  assign xnor_3_out = ~(\电子钟整点报时电路_1_out_16  ^ \电子钟整点报时电路_2_out_16 );  // XNOR_Gate xnor_3, 4 bits wide
  assign xnor_4_out = ~(\电子钟整点报时电路_1_out_12  ^ \电子钟整点报时电路_2_out_12 );  // XNOR_Gate xnor_4, 4 bits wide
  assign xnor_5_out = ~(\电子钟整点报时电路_1_out_13  ^ \电子钟整点报时电路_2_out_13 );  // XNOR_Gate xnor_5, 4 bits wide
  \电子钟整点报时电路  \u_电子钟整点报时电路_2  (
    .in_9(and_6_out), .Hr_minus(and_5_out), .in_4(and_7_out), .Hr_plus(and_4_out), .Min_plus(and_2_out),
    .Min_minus(and_3_out), .in_5(in_9), .out_16(\电子钟整点报时电路_2_out_16 ), .out_15(\电子钟整点报时电路_2_out_15 ),
    .out_12(\电子钟整点报时电路_2_out_12 ), .out_13(\电子钟整点报时电路_2_out_13 ), .AM_FM(\电子钟整点报时电路_2_am_fm ));  // open: Sec_plus, out_14, out_10, out_11, Sec_minus
  assign and_9_out = xnor_2_out & xnor_3_out & xnor_4_out & xnor_5_out;  // AND_Gate and_9, 4 bits wide
  Comparator #(.width(4)) comparator_1 (.a(4'b1111), .b(and_9_out), .eq(comparator_1_eq));  // open: gt, lt
  nor nor_1 (nor_1_out, out_18[3], out_18[1], out_18[2], out_18[0]);
  and and_10 (\闹钟 , ON_OFF, xnor_1_out, comparator_1_eq, nor_1_out, CP);
endmodule

module \闹钟测试电路  (
  input  in_1,
  input  in_2,
  input  in_3,
  input  in_4,
  input  in_5
);

  wire button_1_out, button_2_out, button_3_out, clock_1_out, \闹钟_1_闹钟 ;
  wire [3:0] \闹钟_1_out_14 , \闹钟_1_out_15 , \闹钟_1_out_16 , \闹钟_1_out_17 , \闹钟_1_out_18 , \闹钟_1_out_19 ;
  wire [4:0] \闹钟_1_out_10 , \闹钟_1_out_11 , \闹钟_1_out_12 , \闹钟_1_out_13 ;

  DotMatrix #(.matrixcols(4), .matrixrows(5)) dotmatrix_1 (
    .col0(\闹钟_1_out_10 ), .col1(\闹钟_1_out_11 ), .col2(\闹钟_1_out_12 ), .col3(\闹钟_1_out_13 ));
  Hex_Digit_Display hex_digit_display_1 (.value(\闹钟_1_out_14 ));  // open: dp
  Clock clock_1 (.out(clock_1_out));
  Button button_1 (.out(button_1_out));
  Button button_2 (.out(button_2_out));
  Hex_Digit_Display hex_digit_display_2 (.value(\闹钟_1_out_15 ));  // open: dp
  Hex_Digit_Display hex_digit_display_3 (.value(\闹钟_1_out_16 ));  // open: dp
  Button button_3 (.out(button_3_out));
  Hex_Digit_Display hex_digit_display_4 (.value(\闹钟_1_out_18 ));  // open: dp
  Hex_Digit_Display hex_digit_display_5 (.value(\闹钟_1_out_17 ));  // open: dp
  Hex_Digit_Display hex_digit_display_6 (.value(\闹钟_1_out_19 ));  // open: dp
  \闹钟  \u_闹钟_1  (
    .out_14(\闹钟_1_out_14 ), .out_15(\闹钟_1_out_15 ), .out_16(\闹钟_1_out_16 ), .out_17(\闹钟_1_out_17 ),
    .ON_OFF(in_5), .\闹钟 (\闹钟_1_闹钟 ), .alarm(in_4), .Clr(button_3_out), .Adj0(in_1), .CP(clock_1_out),
    .Adj1(in_2), .CPU(button_2_out), .CPD(button_1_out), .in_9(in_3), .out_18(\闹钟_1_out_18 ),
    .out_19(\闹钟_1_out_19 ), .out_10(\闹钟_1_out_10 ), .out_11(\闹钟_1_out_11 ), .out_12(\闹钟_1_out_12 ),
    .out_13(\闹钟_1_out_13 ));  // open: out_21
  LED led_1 (.in(\闹钟_1_闹钟 ));
endmodule
