// Logisim project 实验六.circ as structural Verilog: 7 circuits, main circuit sqrX
module sqrX (
  input  [31:0] a,
  input  [31:0] b,
  input  [31:0] c,
  input  [31:0] d,
  output [31:0] a_prime,
  output [31:0] b_prime,
  output [31:0] c_prime,
  output [31:0] d_prime
);

  wire [31:0] multiplier_1_out, multiplier_2_out, multiplier_3_out, multiplier_4_out, multiplier_5_out,
       multiplier_6_out, multiplier_7_out;

  Multiplier #(.width(32)) multiplier_1 (.a(a), .b(a), .out(multiplier_1_out));  // open: cin, cout
  Multiplier #(.width(32)) multiplier_2 (.a(a), .b(b), .out(multiplier_2_out));  // open: cin, cout
  Multiplier #(.width(32)) multiplier_3 (.a(a), .b(c), .out(multiplier_3_out));  // open: cin, cout
  Multiplier #(.width(32)) multiplier_4 (.a(b), .b(c), .out(multiplier_4_out));  // open: cin, cout
  Multiplier #(.width(32)) multiplier_5 (.a(b), .b(d), .out(multiplier_5_out));  // open: cin, cout
  Multiplier #(.width(32)) multiplier_6 (.a(c), .b(d), .out(multiplier_6_out));  // open: cin, cout
  Multiplier #(.width(32)) multiplier_7 (.a(d), .b(d), .out(multiplier_7_out));  // open: cin, cout
  Adder #(.width(32)) adder_1 (.a(multiplier_1_out), .b(multiplier_4_out), .out(a_prime));  // open: cin, cout
  Adder #(.width(32)) adder_2 (.a(multiplier_2_out), .b(multiplier_5_out), .out(b_prime));  // open: cin, cout
  Adder #(.width(32)) adder_3 (.a(multiplier_3_out), .b(multiplier_6_out), .out(c_prime));  // open: cin, cout
  Adder #(.width(32)) adder_4 (.a(multiplier_4_out), .b(multiplier_7_out), .out(d_prime));  // open: cin, cout
endmodule

module sqrX_A (
  input  [31:0] a,
  input  [31:0] b,
  input  [31:0] c,
  input  [31:0] d,
  output [31:0] a_prime_prime,
  output [31:0] b_prime_prime,
  output [31:0] c_prime_prime,
  output [31:0] d_prime_prime
);

  wire [31:0] adder_2_out, adder_4_out, multiplier_1_out, multiplier_2_out, multiplier_3_out,
       multiplier_4_out, multiplier_5_out, multiplier_6_out, multiplier_7_out;

  Multiplier #(.width(32)) multiplier_1 (.a(a), .b(b), .out(multiplier_1_out));  // open: cin, cout
  Multiplier #(.width(32)) multiplier_2 (.a(b), .b(d), .out(multiplier_2_out));  // open: cin, cout
  Multiplier #(.width(32)) multiplier_3 (.a(a), .b(a), .out(multiplier_3_out));  // open: cin, cout
  Multiplier #(.width(32)) multiplier_4 (.a(b), .b(c), .out(multiplier_4_out));  // open: cin, cout
  Multiplier #(.width(32)) multiplier_5 (.a(d), .b(d), .out(multiplier_5_out));  // open: cin, cout
  Multiplier #(.width(32)) multiplier_6 (.a(a), .b(c), .out(multiplier_6_out));  // open: cin, cout
  Multiplier #(.width(32)) multiplier_7 (.a(c), .b(d), .out(multiplier_7_out));  // open: cin, cout
  Adder #(.width(32)) adder_1 (.a(multiplier_1_out), .b(multiplier_2_out), .out(a_prime_prime));  // open: cin, cout
  Adder #(.width(32)) adder_2 (.a(multiplier_3_out), .b(multiplier_4_out), .out(adder_2_out));  // open: cin, cout
  Adder #(.width(32)) adder_3 (.a(multiplier_4_out), .b(multiplier_5_out), .out(c_prime_prime));  // open: cin, cout
  Adder #(.width(32)) adder_4 (.a(multiplier_6_out), .b(multiplier_7_out), .out(adder_4_out));  // open: cin, cout
  Adder #(.width(32)) adder_5 (.a(a_prime_prime), .b(adder_2_out), .out(b_prime_prime));  // open: cin, cout
  Adder #(.width(32)) adder_6 (.a(c_prime_prime), .b(adder_4_out), .out(d_prime_prime));  // open: cin, cout
endmodule

module \矩阵快速幂算法迭代模块  (
  input  clk,
  input  start,
  input  n_i_1,
  input  clr,
  output [31:0] out_5
);

  wire and_1_out, not_1_out;
  wire [31:0] multiplexer_1_out, multiplexer_2_out, multiplexer_3_out, multiplexer_4_out, multiplexer_5_out,
       multiplexer_6_out, multiplexer_7_out, multiplexer_8_out, register_1_q, register_3_q, register_4_q,
       sqrx_1_a_prime, sqrx_1_b_prime, sqrx_1_c_prime, sqrx_1_d_prime, sqrx_a_1_a_prime_prime,
       sqrx_a_1_b_prime_prime, sqrx_a_1_c_prime_prime, sqrx_a_1_d_prime_prime;

  Multiplexer #(.width(32), .enable("false")) multiplexer_1 (
    .in0({32{1'b0}}), .in1(multiplexer_5_out), .out(multiplexer_1_out), .sel(and_1_out));
  Multiplexer #(.width(32), .enable("false")) multiplexer_2 (
    .in0(32'h1), .in1(multiplexer_6_out), .out(multiplexer_2_out), .sel(and_1_out));
  Multiplexer #(.width(32), .enable("false")) multiplexer_3 (
    .in0(32'h1), .in1(multiplexer_7_out), .out(multiplexer_3_out), .sel(and_1_out));
  Multiplexer #(.width(32), .enable("false")) multiplexer_4 (
    .in0(32'h1), .in1(multiplexer_8_out), .out(multiplexer_4_out), .sel(and_1_out));
  and and_1 (and_1_out, start, not_1_out);
  not not_1 (not_1_out, clr);
  Register #(.width(32)) register_1 (.D(multiplexer_1_out), .en(1'b1), .Q(register_1_q), .clk(clk), .clr(clr));
  Register #(.width(32)) register_2 (.D(multiplexer_2_out), .en(1'b1), .Q(out_5), .clk(clk), .clr(clr));
  Register #(.width(32)) register_3 (.D(multiplexer_3_out), .en(1'b1), .Q(register_3_q), .clk(clk), .clr(clr));
  Register #(.width(32)) register_4 (.D(multiplexer_4_out), .en(1'b1), .Q(register_4_q), .clk(clk), .clr(clr));
  sqrX sqrx_1 (
    .a(register_1_q), .c(register_3_q), .d(register_4_q), .a_prime(sqrx_1_a_prime), .b_prime(sqrx_1_b_prime),
    .c_prime(sqrx_1_c_prime), .d_prime(sqrx_1_d_prime), .b(out_5));
  sqrX_A sqrx_a_1 (
    .a(register_1_q), .b(out_5), .c(register_3_q), .d(register_4_q), .a_prime_prime(sqrx_a_1_a_prime_prime),
    .b_prime_prime(sqrx_a_1_b_prime_prime), .c_prime_prime(sqrx_a_1_c_prime_prime),
    .d_prime_prime(sqrx_a_1_d_prime_prime));
  Multiplexer #(.width(32), .enable("false")) multiplexer_5 (
    .in0(sqrx_1_a_prime), .in1(sqrx_a_1_a_prime_prime), .out(multiplexer_5_out), .sel(n_i_1));
  Multiplexer #(.width(32), .enable("false")) multiplexer_6 (
    .in0(sqrx_1_b_prime), .in1(sqrx_a_1_b_prime_prime), .out(multiplexer_6_out), .sel(n_i_1));
  Multiplexer #(.width(32), .enable("false")) multiplexer_7 (
    .in0(sqrx_1_c_prime), .in1(sqrx_a_1_c_prime_prime), .out(multiplexer_7_out), .sel(n_i_1));
  Multiplexer #(.width(32), .enable("false")) multiplexer_8 (
    .in0(sqrx_1_d_prime), .in1(sqrx_a_1_d_prime_prime), .out(multiplexer_8_out), .sel(n_i_1));
endmodule

module \Fibonacci数显示模块  (
  input  [31:0] in_1,
  output [3:0] out_2,
  output [3:0] out_3,
  output [3:0] out_4,
  output [3:0] out_5,
  output [3:0] out_6,
  output [3:0] out_7,
  output [3:0] out_8,
  output [3:0] out_9,
  output [3:0] out_10,
  output [3:0] out_11
);

  wire [31:0] divider_1_rem, divider_2_rem, divider_3_rem, divider_4_rem, divider_5_rem, divider_6_rem,
       divider_7_rem, divider_8_rem;
  wire [31:4] divider_1_out, divider_2_out, divider_3_out, divider_4_out, divider_5_out, divider_6_out,
       divider_7_out, divider_8_out, divider_9_out, divider_9_rem;

  Divider #(.width(32)) divider_1 (
    .a(in_1), .b(32'h3b9aca00), .out({divider_1_out, out_2}), .rem(divider_1_rem));  // open: upper
  Divider #(.width(32)) divider_2 (
    .a(divider_1_rem), .b(32'h5f5e100), .out({divider_2_out, out_3}), .rem(divider_2_rem));  // open: upper
  Divider #(.width(32)) divider_3 (
    .a(divider_2_rem), .b(32'h989680), .out({divider_3_out, out_4}), .rem(divider_3_rem));  // open: upper
  Divider #(.width(32)) divider_4 (
    .a(divider_3_rem), .b(32'hf4240), .out({divider_4_out, out_5}), .rem(divider_4_rem));  // open: upper
  Divider #(.width(32)) divider_5 (
    .a(divider_4_rem), .b(32'h186a0), .out({divider_5_out, out_6}), .rem(divider_5_rem));  // open: upper
  Divider #(.width(32)) divider_6 (
    .a(divider_5_rem), .b(32'h2710), .out({divider_6_out, out_7}), .rem(divider_6_rem));  // open: upper
  Divider #(.width(32)) divider_7 (
    .a(divider_6_rem), .b(32'h3e8), .out({divider_7_out, out_8}), .rem(divider_7_rem));  // open: upper
  Divider #(.width(32)) divider_8 (
    .a(divider_7_rem), .b(32'h64), .out({divider_8_out, out_9}), .rem(divider_8_rem));  // open: upper
  Divider #(.width(32)) divider_9 (
    .a(divider_8_rem), .b(32'ha), .out({divider_9_out, out_10}), .rem({divider_9_rem, out_11}));  // open: upper
endmodule

module \斐波那契_Fibonacci_数列计算器  (
  input  [5:0] in_1,
  input  in_2,
  input  in_3,
  output [3:0] out_4,
  output [3:0] out_5,
  output [3:0] out_6,
  output [3:0] out_7,
  output [3:0] out_8,
  output [3:0] out_9,
  output [3:0] out_10,
  output [3:0] out_11,
  output [3:0] out_12,
  output [3:0] out_13
);

  wire \控制器_1_clk , \控制器_1_clr , \控制器_1_n_i_1 , \控制器_1_start ;
  wire [31:0] \矩阵快速幂算法迭代模块_1_out_5 ;

  \控制器  \u_控制器_1  (
    .clock(in_2), .clear(in_3), .clk(\控制器_1_clk ), .start(\控制器_1_start ), .clr(\控制器_1_clr ),
    .n_i_1(\控制器_1_n_i_1 ), .n(in_1));
  \矩阵快速幂算法迭代模块  \u_矩阵快速幂算法迭代模块_1  (
    .clr(\控制器_1_clr ), .start(\控制器_1_start ), .clk(\控制器_1_clk ), .out_5(\矩阵快速幂算法迭代模块_1_out_5 ),
    .n_i_1(\控制器_1_n_i_1 ));
  \Fibonacci数显示模块  \fibonacci数显示模块_1  (
    .in_1(\矩阵快速幂算法迭代模块_1_out_5 ), .out_2(out_4), .out_3(out_5), .out_4(out_6), .out_5(out_7), .out_6(out_8),
    .out_7(out_9), .out_8(out_10), .out_9(out_11), .out_10(out_12), .out_11(out_13));
endmodule

module \斐波那契_Fibonacci_数列计算器验证电路  (
  input  [5:0] in_1
);

  wire button_1_out, button_2_out;
  wire [3:0] \斐波那契_fibonacci_数列计算器_1_out_4 , \斐波那契_fibonacci_数列计算器_1_out_5 , \斐波那契_fibonacci_数列计算器_1_out_6 ,
       \斐波那契_fibonacci_数列计算器_1_out_7 , \斐波那契_fibonacci_数列计算器_1_out_8 , \斐波那契_fibonacci_数列计算器_1_out_9 ,
       \斐波那契_fibonacci_数列计算器_1_out_10 , \斐波那契_fibonacci_数列计算器_1_out_11 , \斐波那契_fibonacci_数列计算器_1_out_12 ,
       \斐波那契_fibonacci_数列计算器_1_out_13 ;

  Button button_1 (.out(button_1_out));
  Button button_2 (.out(button_2_out));
  \斐波那契_Fibonacci_数列计算器  \u_斐波那契_fibonacci_数列计算器_1  (
    .in_1(in_1), .in_2(button_1_out), .in_3(button_2_out), .out_4(\斐波那契_fibonacci_数列计算器_1_out_4 ),
    .out_5(\斐波那契_fibonacci_数列计算器_1_out_5 ), .out_6(\斐波那契_fibonacci_数列计算器_1_out_6 ),
    .out_7(\斐波那契_fibonacci_数列计算器_1_out_7 ), .out_8(\斐波那契_fibonacci_数列计算器_1_out_8 ),
    .out_9(\斐波那契_fibonacci_数列计算器_1_out_9 ), .out_10(\斐波那契_fibonacci_数列计算器_1_out_10 ),
    .out_11(\斐波那契_fibonacci_数列计算器_1_out_11 ), .out_12(\斐波那契_fibonacci_数列计算器_1_out_12 ),
    .out_13(\斐波那契_fibonacci_数列计算器_1_out_13 ));
  Hex_Digit_Display hex_digit_display_1 (.value(\斐波那契_fibonacci_数列计算器_1_out_4 ));  // open: dp
  Hex_Digit_Display hex_digit_display_2 (.value(\斐波那契_fibonacci_数列计算器_1_out_5 ));  // open: dp
  Hex_Digit_Display hex_digit_display_3 (.value(\斐波那契_fibonacci_数列计算器_1_out_6 ));  // open: dp
  Hex_Digit_Display hex_digit_display_4 (.value(\斐波那契_fibonacci_数列计算器_1_out_7 ));  // open: dp
  Hex_Digit_Display hex_digit_display_5 (.value(\斐波那契_fibonacci_数列计算器_1_out_8 ));  // open: dp
  Hex_Digit_Display hex_digit_display_6 (.value(\斐波那契_fibonacci_数列计算器_1_out_10 ));  // open: dp
  Hex_Digit_Display hex_digit_display_7 (.value(\斐波那契_fibonacci_数列计算器_1_out_9 ));  // open: dp
  Hex_Digit_Display hex_digit_display_8 (.value(\斐波那契_fibonacci_数列计算器_1_out_11 ));  // open: dp
  Hex_Digit_Display hex_digit_display_9 (.value(\斐波那契_fibonacci_数列计算器_1_out_12 ));  // open: dp
  Hex_Digit_Display hex_digit_display_10 (.value(\斐波那契_fibonacci_数列计算器_1_out_13 ));  // open: dp
endmodule

module \控制器  (
  input  clock,
  input  clear,
  input  [5:0] n,
  output clk,
  output start,
  output clr,
  output n_i_1
);

  wire comparator_1_lt, not_1_out, or_1_out, or_2_out;
  wire [7:0] counter_1_q;

  Counter counter_1 (.D(8'h1), .Q(counter_1_q), .clk(clock), .clr(clear));  // open: load, count, carry
  or or_1 (or_1_out, clock, clear);
  not not_1 (not_1_out, clear);
  Shift_Register #(.length(6)) shift_register_1 (
    .shift(not_1_out), .in(1'b0), .clk(or_1_out), .out(n_i_1), .load(clear), .d0(n[0]), .d1(n[1]), .d2(n[2]),
    .d3(n[3]), .d4(n[4]), .d5(n[5]));  // open: clr, q0, q1, q2, q3, q4, q5
  Comparator comparator_1 (.a(counter_1_q), .b(8'h6), .lt(comparator_1_lt));  // open: gt, eq
  and and_1 (clk, comparator_1_lt, clock);
  or or_2 (or_2_out, start, n_i_1);
  D_Flip_Flop d_ff_1 (.clk(clock), .D(or_2_out), .Q(start), .reset(clear));  // open: Qn, preset, en

  assign clr = clear;
endmodule
