// Logisim project 实验四.circ as structural Verilog
module \先行进位并行加法器  (
  input  C0,
  input  A0,
  input  B0,
  input  A1,
  input  B1,
  input  A2,
  input  B2,
  input  A3,
  input  B3,
  output S0,
  output S1,
  output S2,
  output S3,
  output C4
);

  wire and_1_out, and_2_out, and_3_out, and_4_out, and_5_out, and_6_out, and_7_out, and_8_out, and_9_out,
       and_10_out, C1_out, C2_out, C3_out, G0_out, G1_out, G2_out, G3_out, P0_out, P1_out, P2_out, P3_out;

  xor P0 (P0_out, A0, B0);
  and G0 (G0_out, A0, B0);
  xor P1 (P1_out, A1, B1);
  and G1 (G1_out, A1, B1);
  xor P2 (P2_out, A2, B2);
  and G2 (G2_out, A2, B2);
  xor P3 (P3_out, A3, B3);
  and G3 (G3_out, A3, B3);
  and and_1 (and_1_out, C0, P0_out);
  and and_2 (and_2_out, C0, P0_out, P1_out);
  and and_3 (and_3_out, P1_out, G0_out);
  and and_4 (and_4_out, C0, P0_out, P1_out, P2_out);
  and and_5 (and_5_out, P1_out, P2_out, G0_out);
  and and_6 (and_6_out, P2_out, G1_out);
  and and_7 (and_7_out, P2_out, P1_out, P0_out, C0, P3_out);
  and and_8 (and_8_out, G0_out, P3_out, P2_out, P1_out);
  and and_9 (and_9_out, G1_out, P3_out, P2_out);
  and and_10 (and_10_out, G2_out, P3_out);
  or C1 (C1_out, and_1_out, G0_out);
  or C2 (C2_out, and_2_out, and_3_out, G1_out);
  or C3 (C3_out, and_4_out, and_5_out, and_6_out, G2_out);
  or u_C4 (C4, and_7_out, and_8_out, and_9_out, and_10_out, G3_out);
  xor u_S0 (S0, C0, P0_out);
  xor u_S1 (S1, C1_out, P1_out);
  xor u_S2 (S2, C2_out, P2_out);
  xor u_S3 (S3, C3_out, P3_out);
endmodule

module \四位二进制可逆计数器  (
  input  CLR,
  input  CPD,
  input  CPU,
  output Q3,
  output Q2,
  output Q1,
  output Q0
);

  wire and_1_out, and_2_out, and_3_out, and_4_out, and_5_out, and_6_out, d_ff_1_qn, d_ff_2_qn, d_ff_3_qn,
       d_ff_4_qn, not_1_out, or_1_out, or_2_out, or_3_out, or_4_out;

  or or_1 (or_1_out, and_1_out, and_2_out);
  and and_1 (and_1_out, CPU, Q0, Q1, Q2);
  and and_2 (and_2_out, CPD, d_ff_4_qn, d_ff_3_qn, d_ff_2_qn);
  D_Flip_Flop d_ff_1 (
    .clk(or_1_out), .D(d_ff_1_qn), .Q(Q3), .Qn(d_ff_1_qn), .preset(not_1_out), .en(1'b1), .reset(CLR));
  or or_2 (or_2_out, and_4_out, and_3_out);
  and and_3 (and_3_out, CPD, d_ff_4_qn, d_ff_3_qn);
  and and_4 (and_4_out, CPU, Q0, Q1);
  D_Flip_Flop d_ff_2 (
    .clk(or_2_out), .D(d_ff_2_qn), .Q(Q2), .Qn(d_ff_2_qn), .preset(not_1_out), .en(1'b1), .reset(CLR));
  and and_5 (and_5_out, CPU, Q0);
  or or_3 (or_3_out, and_5_out, and_6_out);
  and and_6 (and_6_out, CPD, d_ff_4_qn);
  D_Flip_Flop d_ff_3 (
    .clk(or_3_out), .D(d_ff_3_qn), .Q(Q1), .Qn(d_ff_3_qn), .preset(not_1_out), .en(1'b1), .reset(CLR));
  or or_4 (or_4_out, CPU, CPD);
  D_Flip_Flop d_ff_4 (
    .clk(or_4_out), .D(d_ff_4_qn), .Q(Q0), .Qn(d_ff_4_qn), .preset(not_1_out), .en(1'b1), .reset(CLR));
  not not_1 (not_1_out, 1'b1);
endmodule

module \四位二进制可逆计数器测试电路  (
  input  in_1,
  input  in_2,
  input  in_3,
  output out_4,
  output out_5,
  output out_6,
  output out_7
);

  \四位二进制可逆计数器  \u_四位二进制可逆计数器_1  (.CLR(in_1), .CPD(in_2), .CPU(in_3), .Q3(out_4), .Q2(out_5), .Q1(out_6), .Q0(out_7));
endmodule
